# Fritzing sketch unoshield (saved by Fritzing 0.9.3b)
circuit board: 8.13742cm x 6.55696cm

parts:
  Part1 = Arduino Uno (Rev3) - ICSP
  J3 = female pin header, 2 pins [form="♀ (female)"]
  J4 = female pin header, 2 pins [form="♀ (female)"]
  Part2 = Triple Axis Magnetometer - HMC5883 Breakout

nets (from the pcb view):
  N1: Part1.A4/SDA, Part2.SDA
  N2: Part1.A5/SCL, Part2.SCL
  N3: Part1.ICSP_MISO, Part1.D12/MISO
  5V: Part1.5V, Part2.VCC
  N4: Part1.ICSP_MOSI, Part1.D11_PWM/MOSI, J3.pin1
  GND: Part1.GND, J4.pin2, Part2.GND
  N5: Part1.D10_PWM/SS, J3.pin2
